# Fritzing sketch Guzheng (saved by Fritzing 0.9.3b)
breadboards: 2

parts:
  Part1 = Arduino Uno (Rev3)
  U1 = 74HC4051 [package=so16]
  VCC1 = Battery
  LED1 = LED - 5mm [color="Red (633nm)" package="5 mm [THT]"]
  R1 = Photocell (LDR) [package=THT]
  R2 = Resistor [tolerance=±5% resistance=220 package=THT]

nets:
  N1: Part1.A0, U1.IO
  N2: Part1.D2, U1.A
  N3: Part1.D3_PWM, U1.B
  N4: Part1.D4, U1.C
  5V: Part1.5V, U1.VDD, R2.Pin_0
  N5: Part1.GND, U1.INH, U1.VEE, R1.pin_1
  N6: U1.IO0, R1.pin_0, R2.Pin_1
  N7: VCC1.+, LED1.cathode, LED1.anode

notes:
  The laser
